// Logisim project A.L.U.circ as structural Verilog
module A_L_U (
  input  S0,
  input  S1,
  input  S2,
  input  S3,
  input  B3_O_B3,
  input  A3_O_A3,
  input  B2_O_B2,
  input  A2_O_A2,
  input  B1O_B1,
  input  B0_O_B0,
  input  A1_O_A1,
  input  A0_O_A0,
  input  M,
  input  Cn_or__Cn,
  output G_or_Y,
  output Cn_4_or__Cn_4,
  output P_or_X,
  output F3_or_F3,
  output F2_or_F2,
  output A___B,
  output F1_or_F1,
  output F0_or_F0
);

  wire and_1_out, and_2_out, and_3_out, and_4_out, and_5_out, and_6_out, and_7_out, and_8_out, and_9_out,
       and_10_out, and_11_out, and_12_out, and_13_out, and_14_out, and_15_out, and_16_out, and_17_out,
       and_18_out, and_19_out, and_20_out, and_22_out, and_23_out, and_24_out, and_25_out, and_26_out,
       and_27_out, and_28_out, and_29_out, and_30_out, and_31_out, nor_1_out, nor_2_out, nor_3_out,
       nor_4_out, nor_5_out, nor_6_out, nor_7_out, nor_8_out, nor_10_out, nor_11_out, nor_12_out, not_1_out,
       not_2_out, not_3_out, not_4_out, not_5_out, xor_1_out, xor_2_out, xor_3_out, xor_4_out;

  not not_1 (not_1_out, B3_O_B3);
  not not_2 (not_2_out, B2_O_B2);
  not not_3 (not_3_out, B1O_B1);
  not not_4 (not_4_out, A1_O_A1);
  and and_1 (and_1_out, B3_O_B3, S3, A3_O_A3);
  and and_2 (and_2_out, A3_O_A3, S2, not_1_out);
  and and_3 (and_3_out, not_1_out, S1);
  and and_4 (and_4_out, S0, B3_O_B3);
  and and_5 (and_5_out, B2_O_B2, S3, A2_O_A2);
  and and_6 (and_6_out, A2_O_A2, S2, not_2_out);
  and and_7 (and_7_out, not_2_out, S1);
  and and_8 (and_8_out, S0, B2_O_B2);
  and and_9 (and_9_out, B1O_B1, S3, B0_O_B0);
  and and_10 (and_10_out, B0_O_B0, S2, not_3_out);
  and and_11 (and_11_out, not_3_out, S1);
  and and_12 (and_12_out, S0, B1O_B1);
  and and_13 (and_13_out, A1_O_A1, S3, A0_O_A0);
  and and_14 (and_14_out, A0_O_A0, S2, not_4_out);
  and and_15 (and_15_out, not_4_out, S1);
  and and_16 (and_16_out, S0, A1_O_A1);
  not not_5 (not_5_out, M);
  nor nor_1 (nor_1_out, and_1_out, and_2_out);
  nor nor_2 (nor_2_out, and_3_out, and_4_out, A3_O_A3);
  nor nor_3 (nor_3_out, and_5_out, and_6_out);
  nor nor_4 (nor_4_out, and_7_out, and_8_out, A2_O_A2);
  nor nor_5 (nor_5_out, and_9_out, and_10_out);
  nor nor_6 (nor_6_out, and_11_out, and_12_out, B0_O_B0);
  nor nor_7 (nor_7_out, and_13_out, and_14_out);
  nor nor_8 (nor_8_out, and_15_out, and_16_out, A0_O_A0);
  xor xor_1 (xor_1_out, nor_1_out, nor_2_out);
  xor xor_2 (xor_2_out, nor_3_out, nor_4_out);
  xor xor_3 (xor_3_out, nor_7_out, nor_8_out);
  xor xor_4 (xor_4_out, nor_5_out, nor_6_out);
  and and_17 (and_17_out, nor_1_out, nor_4_out);
  and and_18 (and_18_out, nor_1_out, nor_3_out, nor_6_out);
  and and_19 (and_19_out, nor_1_out, nor_3_out, nor_5_out, nor_8_out);
  and and_20 (and_20_out, nor_1_out, nor_3_out, nor_5_out, nor_7_out, Cn_or__Cn);
  and and_21 (P_or_X, nor_1_out, nor_3_out, nor_5_out, nor_7_out);
  and and_22 (and_22_out, Cn_or__Cn, nor_7_out, nor_5_out, nor_3_out, not_5_out);
  and and_23 (and_23_out, nor_5_out, nor_3_out, nor_8_out, not_5_out);
  and and_24 (and_24_out, nor_3_out, nor_6_out, not_5_out);
  and and_25 (and_25_out, nor_4_out, not_5_out);
  and and_26 (and_26_out, Cn_or__Cn, nor_7_out, nor_5_out, not_5_out);
  and and_27 (and_27_out, nor_5_out, nor_8_out, not_5_out);
  and and_28 (and_28_out, nor_6_out, not_5_out);
  and and_29 (and_29_out, Cn_or__Cn, nor_7_out, not_5_out);
  and and_30 (and_30_out, nor_8_out, not_5_out);
  and and_31 (and_31_out, Cn_or__Cn, not_5_out);
  nor nor_9 (G_or_Y, nor_2_out, and_17_out, and_18_out, and_19_out);
  xor xor_5 (F3_or_F3, xor_1_out, nor_10_out);
  nor nor_10 (nor_10_out, and_22_out, and_23_out, and_24_out, and_25_out);
  nor nor_11 (nor_11_out, and_26_out, and_27_out, and_28_out);
  nor nor_12 (nor_12_out, and_29_out, and_30_out);
  or or_1 (Cn_4_or__Cn_4, G_or_Y, and_20_out);
  xor xor_6 (F2_or_F2, xor_2_out, nor_11_out);
  xor xor_7 (F1_or_F1, xor_4_out, nor_12_out);
  xor xor_8 (F0_or_F0, xor_3_out, and_31_out);
  and and_32 (A___B, F3_or_F3, F2_or_F2, F1_or_F1, F0_or_F0);
endmodule
